// Logisim project 32-bit computer.circ as structural Verilog
module Control_Unit (
  input  [31:0] DATA_IN,
  input  RESET,
  input  CLOCK,
  output OUT_CLOCK,
  output [31:0] DATA_OUT,
  output LOAD,
  output [4:0] MAR_OUT,
  output STORE
);

  wire ACC_MBR, ADD, ALU_ADD, ALU_AND, ALU_SUB, AND, and_25_out, BSB, BUN, CHANGE_0, CHANGE_1, CNG_OPCODE,
       DEC, decoder_2_out10, decoder_2_out11, decoder_2_out12, decoder_2_out13, decoder_2_out14,
       decoder_2_out15, fetch, FLAGS_REG, HLT, ISZ, JN, JZ, LOD, MBR_ACC, MBR_INC, MBR_IR, MBR_MAR,
       MBR_MEM_1, MBR_MEM_2, MBR_MEM_3, MBR_MEM_4, MBR_PC_1, MBR_PC_2, MBR_PC_3, MBR_ZERO, MEM_MBR_1,
       MEM_MBR_2, not_1_out, not_2_out, not_3_out, not_4_out, or_2_out, or_3_out, or_4_out, or_6_out,
       or_7_out, or_8_out, or_9_out, or_10_out, or_11_out, or_12_out, or_13_out, or_14_out, PC_INC_2, PC_MAR,
       ROL, STO, t0, t1, t2, t3;
  wire [1:0] counter_1_q;
  wire [3:0] bit_extender_1_out, FLAG_IN, FLAG_OUT, IR_OUT;
  wire [4:0] ADDRESS, multiplexer_1_out, multiplexer_5_out;
  wire [31:0] ACC_IN, ACC_OUT, multiplexer_2_out, multiplexer_3_out, multiplexer_4_out, multiplexer_7_out,
       n32_bit_alu_1_result, NEW_MBR, rol_1_out;
  wire [31:5] MBR_OUT;

  Counter #(.width(2), .max('h3)) counter_1 (
    .Q(counter_1_q), .clk(OUT_CLOCK), .clr(RESET));  // open: load, D, count, carry
  not not_1 (not_1_out, fetch);
  not not_2 (not_2_out, fetch);
  not not_3 (not_3_out, fetch);
  or or_1 (LOAD, MEM_MBR_1, MEM_MBR_2);
  or or_2 (or_2_out, MEM_MBR_1, PC_INC_2, MBR_MEM_1);
  or or_3 (or_3_out, MBR_PC_1, MBR_PC_2, MBR_PC_3);
  Multiplexer #(.width(5), .enable("false")) multiplexer_1 (
    .in0(NEW_MBR[4:0]), .in1(ADDRESS), .out(multiplexer_1_out), .sel(MBR_MAR));
  Multiplexer #(.width(32), .enable("false")) multiplexer_2 (
    .in0({MBR_OUT, ADDRESS}), .in1(32'h1), .out(multiplexer_2_out), .sel(ALU_SUB));
  Multiplexer #(.width(32), .enable("false")) multiplexer_3 (
    .in0(ACC_IN), .in1({MBR_OUT, ADDRESS}), .out(multiplexer_3_out), .sel(MBR_ACC));
  or or_4 (or_4_out, ALU_SUB, ALU_ADD, ALU_AND, MBR_ACC);
  ROL rol_1 (.IN({MBR_OUT, ADDRESS}), .OUT(rol_1_out));
  or or_5 (STORE, MBR_MEM_1, MBR_MEM_2, MBR_MEM_3, MBR_MEM_4);
  and and_1 (CHANGE_0, fetch, t3);
  Decoder #(.select(2), .enable("false")) decoder_1 (.out0(t0), .out1(t1), .out2(t2), .out3(t3), .sel(counter_1_q));
  Decoder #(.select(4), .enable("false")) decoder_2 (
    .out0(AND), .out1(ADD), .out2(STO), .out3(ISZ), .out4(BSB), .out5(BUN), .out6(LOD), .out7(HLT),
    .out8(ROL), .out9(DEC), .out10(decoder_2_out10), .out11(decoder_2_out11), .out12(decoder_2_out12),
    .out13(decoder_2_out13), .out14(decoder_2_out14), .out15(decoder_2_out15), .sel(IR_OUT));
  and and_2 (PC_MAR, not_1_out, t0);
  and and_3 (MEM_MBR_1, not_2_out, t1);
  and and_4 (MBR_IR, not_3_out, t2);
  or or_6 (or_6_out, AND, ADD, STO, ISZ, BSB, LOD, HLT, DEC, ROL);
  and and_5 (MBR_PC_1, BUN, t3);
  and and_6 (MBR_MAR, fetch, t0);
  or or_7 (or_7_out, AND, ADD, ISZ, LOD, DEC, ROL);
  and and_7 (ALU_AND, fetch, t2, AND);
  and and_8 (ALU_ADD, fetch, t2, ADD);
  and and_9 (ACC_MBR, fetch, t2, STO);
  and and_10 (MBR_MEM_3, fetch, t3, STO);
  and and_11 (MBR_INC, fetch, t2, ISZ);
  and and_12 (MBR_MEM_2, fetch, t3, ISZ);
  and and_13 (PC_INC_2, fetch, t3, MBR_ZERO, ISZ);
  and and_14 (CNG_OPCODE, fetch, t2, BSB);
  and and_15 (MBR_MEM_1, fetch, t3, BSB);
  and and_16 (MBR_ACC, fetch, t2, LOD);
  and and_17 (ALU_SUB, fetch, t0, DEC);
  and and_18 (MBR_MEM_4, fetch, t3, ROL);
  and and_19 (FLAG_OUT[2], fetch, t2, JZ);
  and and_20 (MBR_PC_2, FLAG_OUT[2], fetch, JZ, t3);
  and and_21 (FLAG_OUT[3], fetch, t2, JN);
  and and_22 (MBR_PC_3, fetch, t3, FLAG_OUT[3], JN);
  and and_23 (OUT_CLOCK, CLOCK, ~HLT);  // AND_Gate
  Multiplexer #(.select(2), .width(32), .enable("false")) multiplexer_4 (
    .in0(DATA_IN), .in1({NEW_MBR[31:28], {23{1'b0}}, NEW_MBR[4:0]}), .in2(ACC_OUT), .out(multiplexer_4_out),
    .sel({ACC_MBR, CNG_OPCODE}));  // open: in3
  Multiplexer #(.width(5), .enable("false")) multiplexer_5 (
    .in0(MAR_OUT), .in1(ADDRESS), .out(multiplexer_5_out), .sel(or_3_out));
  or or_8 (or_8_out, CNG_OPCODE, or_3_out);
  or or_9 (or_9_out, PC_MAR, MBR_MAR);
  _4_bit_IR u_4_bit_ir_1 (.clk(OUT_CLOCK), .clr(RESET), .data(MBR_OUT[31:28]), .load(MBR_IR), .\output (IR_OUT));
  or or_10 (or_10_out, ALU_ADD, ALU_SUB);
  _32_bit_ALU u_32_bit_alu_1 (
    .A(ACC_OUT), .B(multiplexer_2_out), .Result(n32_bit_alu_1_result), .Zero(FLAG_IN[0]),
    .Negative(FLAG_IN[1]), .Carry_Out(FLAG_IN[2]), .Overflow(FLAG_IN[3]), .Control_0(ALU_SUB),
    .Control_1(or_10_out));
  _32_bit_ACC u_32_bit_acc_1 (
    .load(or_4_out), .clk(OUT_CLOCK), .clr(RESET), .data(multiplexer_3_out), .\output (ACC_OUT));
  Register #(.width(4)) register_1 (.D(FLAG_IN), .en(FLAGS_REG), .Q(FLAG_OUT), .clk(OUT_CLOCK), .clr(RESET));
  Multiplexer #(.width(32), .enable("false")) multiplexer_6 (
    .in0(DATA_IN), .in1(multiplexer_7_out), .out(DATA_OUT), .sel(STORE));
  Multiplexer #(.width(32), .enable("false")) multiplexer_7 (
    .in0({MBR_OUT, ADDRESS}), .in1(rol_1_out), .out(multiplexer_7_out), .sel(ROL));
  assign bit_extender_1_out = {{3{CNG_OPCODE}}, CNG_OPCODE};  // Bit_Extender bit_extender_1
  or or_11 (or_11_out, ADDRESS[0], ADDRESS[1], ADDRESS[2], ADDRESS[3], ADDRESS[4], MBR_OUT[5], MBR_OUT[6], MBR_OUT[7], MBR_OUT[8], MBR_OUT[9], MBR_OUT[10], MBR_OUT[11], MBR_OUT[12], MBR_OUT[13], MBR_OUT[14], MBR_OUT[15], MBR_OUT[17], MBR_OUT[18], MBR_OUT[19], MBR_OUT[20], MBR_OUT[21], MBR_OUT[22], MBR_OUT[23], MBR_OUT[24], MBR_OUT[25], MBR_OUT[26], MBR_OUT[27], MBR_OUT[28], MBR_OUT[29], MBR_OUT[30], MBR_OUT[31], MBR_OUT[16]);
  not not_4 (not_4_out, fetch);
  and and_24 (MEM_MBR_2, fetch, t1, or_7_out);
  or or_12 (or_12_out, LOAD, ACC_MBR, CNG_OPCODE);
  _5_bit_PC u_5_bit_pc_1 (
    .cnt(or_2_out), .load(or_8_out), .clk(OUT_CLOCK), .clr(RESET), .data(multiplexer_5_out),
    .\output (NEW_MBR[4:0]));  // open: carry_out
  or or_13 (or_13_out, ALU_AND, or_10_out);
  and and_25 (and_25_out, or_13_out, t2);
  assign NEW_MBR[31:28] = bit_extender_1_out & 4'b0101;  // AND_Gate and_26, 4 bits wide
  not not_5 (MBR_ZERO, or_11_out);
  J_K_Flip_Flop j_k_ff_1 (.J(CHANGE_1), .clk(OUT_CLOCK), .K(CHANGE_0), .Q(fetch));  // open: Qn, preset, en, reset
  and and_27 (CHANGE_1, not_4_out, t3, or_6_out);
  _32_bit_MBR u_32_bit_mbr_1 (
    .data(multiplexer_4_out), .count(MBR_INC), .load(or_12_out), .clk(OUT_CLOCK), .clear(RESET),
    .\output ({MBR_OUT, ADDRESS}));
  _5_bit_MAR u_5_bit_mar_1 (
    .load(or_9_out), .clk(OUT_CLOCK), .clr(RESET), .data(multiplexer_1_out), .\output (MAR_OUT));
  Multiplexer #(.width(32), .enable("false")) multiplexer_8 (
    .in0(ACC_OUT), .in1(n32_bit_alu_1_result), .out(ACC_IN), .sel(or_14_out));
  or or_14 (or_14_out, and_25_out, ALU_SUB);

  // Other names for the same wires on the sheet: MAR_PC = CNG_OPCODE; PC_MBR = CNG_OPCODE; CLOCK_t = OUT_CLOCK;
  //   isZero = FLAG_OUT[2]; isNeg = FLAG_OUT[3]; MBR_OUT[4:0] = ADDRESS; OPCODE[3:0] = MBR_OUT[31:28];
  //   PC_OUT[4:0] = NEW_MBR[4:0]; PC_INC_1 = MEM_MBR_1; PC_INC_3 = MBR_MEM_1

  // Notes on the sheet:
  //   2207053
endmodule

module _32_bit_COMPUTER (
  input  RESET
);

  wire CLOCK_out, control_unit_1_load, control_unit_1_out_clock, control_unit_1_store;
  wire [4:0] control_unit_1_mar_out;
  wire [31:0] control_unit_1_data_out, ram_1_data;

  Clock CLOCK (.out(CLOCK_out));
  Control_Unit control_unit_1 (
    .DATA_IN(ram_1_data), .RESET(RESET), .CLOCK(CLOCK_out), .DATA_OUT(control_unit_1_data_out),
    .OUT_CLOCK(control_unit_1_out_clock), .LOAD(control_unit_1_load), .MAR_OUT(control_unit_1_mar_out),
    .STORE(control_unit_1_store));
  RAM #(.addrWidth(5), .dataWidth(32), .bus("separate")) ram_1 (
    .addr(control_unit_1_mar_out), .din(control_unit_1_data_out), .data(ram_1_data),
    .str(control_unit_1_store), .clk(control_unit_1_out_clock), .ld(control_unit_1_load));  // open: sel, clr

  // Notes on the sheet:
  //   2207053
endmodule
