// Logisim project 32-bit-ALU.circ as structural Verilog: 19 circuits, main circuit main
module main (
  input  [31:0] A,
  input  [31:0] B,
  input  Control_0,
  input  Control_1,
  output [31:0] Result,
  output Zero,
  output Negative,
  output Carry_Out,
  output Overflow
);

  wire [31:0] multiplexer_1_out, n32_bit_add_sub_1_result, n32_bit_and_1_a_b, n32_bit_or_1_a_b;

  _32_bit_and u_32_bit_and_1 (.A(A), .B(B), .A_B(n32_bit_and_1_a_b));
  _32_bit_or u_32_bit_or_1 (.A(A), .B(B), .A_B(n32_bit_or_1_a_b));
  _32_bit_add_sub u_32_bit_add_sub_1 (
    .Result(n32_bit_add_sub_1_result), .carry_out(Carry_Out), .overflow(Overflow), .A(A), .B(B),
    .control(Control_0));
  Multiplexer #(.width(32), .enable("false")) multiplexer_1 (
    .in0(n32_bit_and_1_a_b), .in1(n32_bit_or_1_a_b), .out(multiplexer_1_out), .sel(Control_0));
  Multiplexer #(.width(32), .enable("false")) multiplexer_2 (
    .in0(multiplexer_1_out), .in1(n32_bit_add_sub_1_result), .out({Negative, Result[30:0]}), .sel(Control_1));
  nor nor_1 (Zero, Result[15], Result[0], Result[1], Result[2], Result[3], Result[4], Result[5], Result[6], Result[7], Result[8], Result[9], Result[10], Result[11], Result[12], Result[13], Result[14], Result[16], Result[17], Result[18], Result[19], Result[20], Result[21], Result[22], Result[23], Result[24], Result[25], Result[26], Result[27], Result[28], Result[29], Result[30], Negative);

  assign Result[31] = Negative;

  // Notes on the sheet:
  //   2207053
endmodule

// AND
module _32_bit_and (
  input  [31:0] A,
  input  [31:0] B,
  output [31:0] A_B
);

  assign A_B = A & B;  // AND_Gate and_1, 32 bits wide

  // Notes on the sheet:
  //   2207053
endmodule

// OR
module _32_bit_or (
  input  [31:0] A,
  input  [31:0] B,
  output [31:0] A_B
);

  assign A_B = A | B;  // OR_Gate or_1, 32 bits wide

  // Notes on the sheet:
  //   2207053
endmodule

module _4_bit_clg (
  input  c0,
  input  g0,
  input  p0,
  input  g1,
  input  p1,
  input  g2,
  input  p2,
  input  g3,
  input  p3,
  output c1,
  output c2,
  output c3,
  output c4
);

  wire and_1_out, and_2_out, and_3_out, and_4_out, and_5_out, and_6_out, and_7_out, and_8_out, and_9_out,
       and_10_out;

  and and_1 (and_1_out, p0, c0);
  and and_2 (and_2_out, p1, g0);
  and and_3 (and_3_out, p1, p0, c0);
  and and_4 (and_4_out, p2, g1);
  and and_5 (and_5_out, p2, p1, g0);
  and and_6 (and_6_out, p2, p1, p0, c0);
  and and_7 (and_7_out, p3, g2);
  and and_8 (and_8_out, p3, p2, g1);
  and and_9 (and_9_out, p3, p2, p1, g0);
  and and_10 (and_10_out, p3, p2, p1, p0, c0);
  or or_1 (c1, and_1_out, g0);
  or or_2 (c2, and_2_out, and_3_out, g1);
  or or_3 (c3, and_4_out, and_5_out, and_6_out, g2);
  or or_4 (c4, and_7_out, and_8_out, and_9_out, and_10_out, g3);

  // Notes on the sheet:
  //   2207053
endmodule

// ADD/SUB
module _32_bit_add_sub (
  input  control,
  input  [31:0] A,
  input  [31:0] B,
  output [31:0] Result,
  output carry_out,
  output overflow
);

  wire n4_bit_add_sub_2_c4, n4_bit_add_sub_3_c4, n4_bit_add_sub_4_c4, n4_bit_add_sub_5_c4,
       n4_bit_add_sub_6_c4, n4_bit_add_sub_7_c4, n4_bit_add_sub_8_c4;

  _4_bit_add_sub u_4_bit_add_sub_1 (
    .c4(carry_out), .Result(Result[31:28]), .overflow(overflow), .A(A[31:28]), .B(B[31:28]),
    .control(control), .c0(n4_bit_add_sub_2_c4));
  _4_bit_add_sub u_4_bit_add_sub_2 (
    .c4(n4_bit_add_sub_2_c4), .Result(Result[27:24]), .A(A[27:24]), .B(B[27:24]), .control(control),
    .c0(n4_bit_add_sub_3_c4));  // open: overflow
  _4_bit_add_sub u_4_bit_add_sub_3 (
    .c4(n4_bit_add_sub_3_c4), .Result(Result[23:20]), .A(A[23:20]), .B(B[23:20]), .control(control),
    .c0(n4_bit_add_sub_4_c4));  // open: overflow
  _4_bit_add_sub u_4_bit_add_sub_4 (
    .c4(n4_bit_add_sub_4_c4), .Result(Result[19:16]), .A(A[19:16]), .B(B[19:16]), .control(control),
    .c0(n4_bit_add_sub_5_c4));  // open: overflow
  _4_bit_add_sub u_4_bit_add_sub_5 (
    .c4(n4_bit_add_sub_5_c4), .Result(Result[15:12]), .A(A[15:12]), .B(B[15:12]), .control(control),
    .c0(n4_bit_add_sub_6_c4));  // open: overflow
  _4_bit_add_sub u_4_bit_add_sub_6 (
    .c4(n4_bit_add_sub_6_c4), .Result(Result[11:8]), .A(A[11:8]), .B(B[11:8]), .control(control),
    .c0(n4_bit_add_sub_7_c4));  // open: overflow
  _4_bit_add_sub u_4_bit_add_sub_7 (
    .c4(n4_bit_add_sub_7_c4), .Result(Result[7:4]), .A(A[7:4]), .B(B[7:4]), .control(control),
    .c0(n4_bit_add_sub_8_c4));  // open: overflow
  _4_bit_add_sub u_4_bit_add_sub_8 (
    .c4(n4_bit_add_sub_8_c4), .Result(Result[3:0]), .A(A[3:0]), .B(B[3:0]), .control(control), .c0(control));  // open: overflow

  // Notes on the sheet:
  //   2207053
endmodule

module _4_bit_add_sub (
  input  [3:0] A,
  input  [3:0] B,
  input  control,
  input  c0,
  output c4,
  output [3:0] Result,
  output overflow
);

  wire and_1_out, and_2_out, and_3_out, and_4_out, and_5_out, and_6_out, n4_bit_clg_1_c1, n4_bit_clg_1_c2,
       n4_bit_clg_1_c3, not_1_out, not_2_out, not_3_out, p0, p1, p2, p3, xor_1_out, xor_2_out, xor_3_out,
       xor_4_out, xor_5_out, xor_6_out, xor_7_out, xor_8_out;

  not not_1 (not_1_out, A[3]);
  not not_2 (not_2_out, B[3]);
  not not_3 (not_3_out, Result[3]);
  xor xor_1 (xor_1_out, B[0], control);
  xor xor_2 (xor_2_out, B[0], control);
  xor xor_3 (xor_3_out, B[1], control);
  xor xor_4 (xor_4_out, B[1], control);
  xor xor_5 (xor_5_out, B[2], control);
  xor xor_6 (xor_6_out, B[2], control);
  xor xor_7 (xor_7_out, B[3], control);
  xor xor_8 (xor_8_out, B[3], control);
  and and_1 (and_1_out, not_1_out, not_2_out, Result[3]);
  and and_2 (and_2_out, A[3], B[3], not_3_out);
  and and_3 (and_3_out, A[0], xor_1_out);
  xor xor_9 (p0, A[0], xor_2_out);
  and and_4 (and_4_out, A[1], xor_3_out);
  xor xor_10 (p1, A[1], xor_4_out);
  and and_5 (and_5_out, A[2], xor_5_out);
  xor xor_11 (p2, A[2], xor_6_out);
  and and_6 (and_6_out, A[2], xor_7_out);
  xor xor_12 (p3, A[3], xor_8_out);
  or or_1 (overflow, and_1_out, and_2_out);
  _4_bit_clg u_4_bit_clg_1 (
    .c0(c0), .g0(and_3_out), .p0(p0), .g1(and_4_out), .p1(p1), .g2(and_5_out), .p2(p2), .g3(and_6_out),
    .p3(p3), .c1(n4_bit_clg_1_c1), .c2(n4_bit_clg_1_c2), .c3(n4_bit_clg_1_c3), .c4(c4));
  xor xor_13 (Result[3], p3, n4_bit_clg_1_c3);
  xor xor_14 (Result[2], p2, n4_bit_clg_1_c2);
  xor xor_15 (Result[1], p1, n4_bit_clg_1_c1);
  xor xor_16 (Result[0], p0, c0);

  // Other names for the same wires on the sheet: S3 = Result[3]

  // Notes on the sheet:
  //   2207053
endmodule

module _32_bit_ALU (
  input  [31:0] A,
  input  [31:0] B,
  input  Control_0,
  input  Control_1,
  output [31:0] Result,
  output Zero,
  output Negative,
  output Carry_Out,
  output Overflow
);

  wire n32_bit_add_sub_1_carry_out, n32_bit_add_sub_1_overflow;
  wire [31:0] multiplexer_1_out, n32_bit_add_sub_1_result, n32_bit_and_1_a_b, n32_bit_or_1_a_b;

  _32_bit_and u_32_bit_and_1 (.A(A), .B(B), .A_B(n32_bit_and_1_a_b));
  _32_bit_or u_32_bit_or_1 (.A(A), .B(B), .A_B(n32_bit_or_1_a_b));
  _32_bit_add_sub u_32_bit_add_sub_1 (
    .Result(n32_bit_add_sub_1_result), .carry_out(n32_bit_add_sub_1_carry_out),
    .overflow(n32_bit_add_sub_1_overflow), .A(A), .B(B), .control(Control_0));
  Multiplexer #(.width(32), .enable("false")) multiplexer_1 (
    .in0(n32_bit_and_1_a_b), .in1(n32_bit_or_1_a_b), .out(multiplexer_1_out), .sel(Control_0));
  Multiplexer #(.width(32), .enable("false")) multiplexer_2 (
    .in0(multiplexer_1_out), .in1(n32_bit_add_sub_1_result), .out({Negative, Result[30:0]}), .sel(Control_1));
  nor nor_1 (Zero, Result[15], Result[0], Result[1], Result[2], Result[3], Result[4], Result[5], Result[6], Result[7], Result[8], Result[9], Result[10], Result[11], Result[12], Result[13], Result[14], Result[16], Result[17], Result[18], Result[19], Result[20], Result[21], Result[22], Result[23], Result[24], Result[25], Result[26], Result[27], Result[28], Result[29], Result[30], Negative);
  and and_1 (Carry_Out, n32_bit_add_sub_1_carry_out, Control_1);
  and and_2 (Overflow, n32_bit_add_sub_1_overflow, Control_1);

  assign Result[31] = Negative;

  // Other names for the same wires on the sheet: Con1 = Control_1

  // Notes on the sheet:
  //   2207053
endmodule

module control (
  input  [1:0] Q,
  input  [2:0] T,
  input  C,
  output DA,
  output DB,
  output DC
);

  wire and_1_out, and_2_out, and_3_out, and_4_out, and_5_out, or_1_out, or_2_out, Q0, Q1, Q2, Q3, T0, T1, T2,
       T3, T4, T5, T6, T7;

  or or_1 (or_1_out, Q0, Q2, Q3);
  or or_2 (or_2_out, Q0, Q1, Q3);
  Decoder #(.select(2), .enable("false")) decoder_1 (.out0(Q0), .out1(Q1), .out2(Q2), .out3(Q3), .sel(Q));
  Decoder #(.select(3), .enable("false")) decoder_2 (
    .out0(T0), .out1(T1), .out2(T2), .out3(T3), .out4(T4), .out5(T5), .out6(T6), .out7(T7), .sel(T));
  and and_1 (and_1_out, T2, or_1_out);
  and and_2 (and_2_out, T6, C);
  and and_3 (and_3_out, T2, Q2);
  and and_4 (and_4_out, T2, or_2_out);
  and and_5 (and_5_out, T6, C);
  or or_3 (DA, T0, and_1_out, T3, T4, and_2_out, T7);
  or or_4 (DB, T1, and_3_out, T5, T6, T6, T7);
  or or_5 (DC, T5, and_4_out, T3, T4, and_5_out, T7);

  // Notes on the sheet:
  //   2207053
endmodule

module sequence_detector (
  input  clk,
  input  reset,
  input  Q0,
  input  Q_1,
  input  [5:0] count,
  output CL__A__Q_1,
  output Load__M__Q__Cnt,
  output Load_A,
  output C0,
  output C1,
  output Shr,
  output Dec_Cnt
);

  wire control_1_da, control_1_db, control_1_dc, nor_1_out, T0, T2, T4, T6, T7;
  wire [2:0] T;

  nor nor_1 (nor_1_out, count[0], count[1], count[2], count[4], count[5], count[3]);
  Decoder #(.select(3), .enable("false")) decoder_1 (
    .out0(T0), .out1(CL__A__Q_1), .out2(T2), .out3(C0), .out4(T4), .out5(Dec_Cnt), .out6(T6), .out7(T7),
    .sel(T));
  control control_1 (.Q({Q0, Q_1}), .T(T), .C(nor_1_out), .DA(control_1_da), .DB(control_1_db), .DC(control_1_dc));
  or or_1 (Load_A, C0, T4);
  or or_2 (C1, T4, C0);
  D_Flip_Flop d_ff_1 (.clk(clk), .D(control_1_da), .Q(T[0]), .reset(reset));  // open: Qn, preset, en
  D_Flip_Flop d_ff_2 (.clk(clk), .D(control_1_db), .Q(T[1]), .reset(reset));  // open: Qn, preset, en
  D_Flip_Flop d_ff_3 (.clk(clk), .D(control_1_dc), .Q(T[2]), .reset(reset));  // open: Qn, preset, en

  assign Load__M__Q__Cnt = CL__A__Q_1;
  assign Shr = Dec_Cnt;

  // Other names for the same wires on the sheet: T1 = CL__A__Q_1; T3 = C0; T5 = Dec_Cnt

  // Notes on the sheet:
  //   2207053
endmodule

module booths_multiplier (
  input  [31:0] M,
  input  [31:0] Q,
  input  Reset,
  output [31:0] Result__32_63,
  output [31:0] Result__0_31
);

  wire A_out, CLK_out, or_1_out, Q_1_q0, Q_out, sequence_detector_1_c0, sequence_detector_1_c1,
       sequence_detector_1_cl__a__q_1, sequence_detector_1_dec_cnt, sequence_detector_1_load__m__q__cnt,
       sequence_detector_1_load_a, sequence_detector_1_shr;
  wire [5:0] counter_1_q;
  wire [31:0] M_q31, n32_bit_alu_1_result;

  Clock CLK (.out(CLK_out));
  sequence_detector sequence_detector_1 (
    .clk(CLK_out), .reset(Reset), .Q0(Result__0_31[0]), .Q_1(Q_1_q0), .count(counter_1_q),
    .CL__A__Q_1(sequence_detector_1_cl__a__q_1), .Load__M__Q__Cnt(sequence_detector_1_load__m__q__cnt),
    .Load_A(sequence_detector_1_load_a), .C0(sequence_detector_1_c0), .C1(sequence_detector_1_c1),
    .Shr(sequence_detector_1_shr), .Dec_Cnt(sequence_detector_1_dec_cnt));
  or or_1 (or_1_out, sequence_detector_1_load__m__q__cnt, sequence_detector_1_dec_cnt);
  Counter #(.width(6), .max('h20)) counter_1 (
    .load(or_1_out), .D(6'b100000), .count(sequence_detector_1_dec_cnt), .Q(counter_1_q), .clk(CLK_out));  // open: carry, clr
  Shift_Register #(.length(32)) u_M (
    .shift(1'b0), .clk(CLK_out), .load(sequence_detector_1_load__m__q__cnt), .d0(M[31]), .q0(M_q31[31]),
    .d1(M[30]), .q1(M_q31[30]), .d2(M[29]), .q2(M_q31[29]), .d3(M[28]), .q3(M_q31[28]), .d4(M[27]),
    .q4(M_q31[27]), .d5(M[26]), .q5(M_q31[26]), .d6(M[25]), .q6(M_q31[25]), .d7(M[24]), .q7(M_q31[24]),
    .d8(M[23]), .q8(M_q31[23]), .d9(M[22]), .q9(M_q31[22]), .d10(M[21]), .q10(M_q31[21]), .d11(M[20]),
    .q11(M_q31[20]), .d12(M[19]), .q12(M_q31[19]), .d13(M[18]), .q13(M_q31[18]), .d14(M[17]),
    .q14(M_q31[17]), .d15(M[16]), .q15(M_q31[16]), .d16(M[15]), .q16(M_q31[15]), .d17(M[14]),
    .q17(M_q31[14]), .d18(M[13]), .q18(M_q31[13]), .d19(M[12]), .q19(M_q31[12]), .d20(M[11]),
    .q20(M_q31[11]), .d21(M[10]), .q21(M_q31[10]), .d22(M[9]), .q22(M_q31[9]), .d23(M[8]), .q23(M_q31[8]),
    .d24(M[7]), .q24(M_q31[7]), .d25(M[6]), .q25(M_q31[6]), .d26(M[5]), .q26(M_q31[5]), .d27(M[4]),
    .q27(M_q31[4]), .d28(M[3]), .q28(M_q31[3]), .d29(M[2]), .q29(M_q31[2]), .d30(M[1]), .q30(M_q31[1]),
    .d31(M[0]), .q31(M_q31[0]));  // open: in, out, clr
  Shift_Register #(.length(32)) A (
    .shift(sequence_detector_1_shr), .in(Result__32_63[31]), .clk(CLK_out), .out(A_out),
    .load(sequence_detector_1_load_a), .clr(sequence_detector_1_cl__a__q_1), .d0(n32_bit_alu_1_result[31]),
    .q0(Result__32_63[31]), .d1(n32_bit_alu_1_result[30]), .q1(Result__32_63[30]),
    .d2(n32_bit_alu_1_result[29]), .q2(Result__32_63[29]), .d3(n32_bit_alu_1_result[28]),
    .q3(Result__32_63[28]), .d4(n32_bit_alu_1_result[27]), .q4(Result__32_63[27]),
    .d5(n32_bit_alu_1_result[26]), .q5(Result__32_63[26]), .d6(n32_bit_alu_1_result[25]),
    .q6(Result__32_63[25]), .d7(n32_bit_alu_1_result[24]), .q7(Result__32_63[24]),
    .d8(n32_bit_alu_1_result[23]), .q8(Result__32_63[23]), .d9(n32_bit_alu_1_result[22]),
    .q9(Result__32_63[22]), .d10(n32_bit_alu_1_result[21]), .q10(Result__32_63[21]),
    .d11(n32_bit_alu_1_result[20]), .q11(Result__32_63[20]), .d12(n32_bit_alu_1_result[19]),
    .q12(Result__32_63[19]), .d13(n32_bit_alu_1_result[18]), .q13(Result__32_63[18]),
    .d14(n32_bit_alu_1_result[17]), .q14(Result__32_63[17]), .d15(n32_bit_alu_1_result[16]),
    .q15(Result__32_63[16]), .d16(n32_bit_alu_1_result[15]), .q16(Result__32_63[15]),
    .d17(n32_bit_alu_1_result[14]), .q17(Result__32_63[14]), .d18(n32_bit_alu_1_result[13]),
    .q18(Result__32_63[13]), .d19(n32_bit_alu_1_result[12]), .q19(Result__32_63[12]),
    .d20(n32_bit_alu_1_result[11]), .q20(Result__32_63[11]), .d21(n32_bit_alu_1_result[10]),
    .q21(Result__32_63[10]), .d22(n32_bit_alu_1_result[9]), .q22(Result__32_63[9]),
    .d23(n32_bit_alu_1_result[8]), .q23(Result__32_63[8]), .d24(n32_bit_alu_1_result[7]),
    .q24(Result__32_63[7]), .d25(n32_bit_alu_1_result[6]), .q25(Result__32_63[6]),
    .d26(n32_bit_alu_1_result[5]), .q26(Result__32_63[5]), .d27(n32_bit_alu_1_result[4]),
    .q27(Result__32_63[4]), .d28(n32_bit_alu_1_result[3]), .q28(Result__32_63[3]),
    .d29(n32_bit_alu_1_result[2]), .q29(Result__32_63[2]), .d30(n32_bit_alu_1_result[1]),
    .q30(Result__32_63[1]), .d31(n32_bit_alu_1_result[0]), .q31(Result__32_63[0]));
  _32_bit_ALU u_32_bit_alu_1 (
    .A(Result__32_63), .B(M_q31), .Result(n32_bit_alu_1_result), .Control_0(sequence_detector_1_c0),
    .Control_1(sequence_detector_1_c1));  // open: Zero, Negative, Carry_Out, Overflow
  Shift_Register #(.length(32)) u_Q (
    .shift(sequence_detector_1_shr), .in(A_out), .clk(CLK_out), .out(Q_out),
    .load(sequence_detector_1_load__m__q__cnt), .d0(Q[31]), .q0(Result__0_31[31]), .d1(Q[30]),
    .q1(Result__0_31[30]), .d2(Q[29]), .q2(Result__0_31[29]), .d3(Q[28]), .q3(Result__0_31[28]), .d4(Q[27]),
    .q4(Result__0_31[27]), .d5(Q[26]), .q5(Result__0_31[26]), .d6(Q[25]), .q6(Result__0_31[25]), .d7(Q[24]),
    .q7(Result__0_31[24]), .d8(Q[23]), .q8(Result__0_31[23]), .d9(Q[22]), .q9(Result__0_31[22]), .d10(Q[21]),
    .q10(Result__0_31[21]), .d11(Q[20]), .q11(Result__0_31[20]), .d12(Q[19]), .q12(Result__0_31[19]),
    .d13(Q[18]), .q13(Result__0_31[18]), .d14(Q[17]), .q14(Result__0_31[17]), .d15(Q[16]),
    .q15(Result__0_31[16]), .d16(Q[15]), .q16(Result__0_31[15]), .d17(Q[14]), .q17(Result__0_31[14]),
    .d18(Q[13]), .q18(Result__0_31[13]), .d19(Q[12]), .q19(Result__0_31[12]), .d20(Q[11]),
    .q20(Result__0_31[11]), .d21(Q[10]), .q21(Result__0_31[10]), .d22(Q[9]), .q22(Result__0_31[9]),
    .d23(Q[8]), .q23(Result__0_31[8]), .d24(Q[7]), .q24(Result__0_31[7]), .d25(Q[6]), .q25(Result__0_31[6]),
    .d26(Q[5]), .q26(Result__0_31[5]), .d27(Q[4]), .q27(Result__0_31[4]), .d28(Q[3]), .q28(Result__0_31[3]),
    .d29(Q[2]), .q29(Result__0_31[2]), .d30(Q[1]), .q30(Result__0_31[1]), .d31(Q[0]), .q31(Result__0_31[0]));  // open: clr
  Shift_Register #(.length(1)) Q_1 (
    .shift(sequence_detector_1_shr), .in(Q_out), .clk(CLK_out), .clr(sequence_detector_1_cl__a__q_1),
    .q0(Q_1_q0));  // open: out, load, d0

  // Notes on the sheet:
  //   2207053
endmodule

// 4-bit plr
module _4_bit_parallel_load_register (
  input  load,
  input  [3:0] data,
  input  clk,
  input  clr,
  output [3:0] \output 
);

  wire and_1_out, and_2_out, and_3_out, and_4_out, and_5_out, and_6_out, and_7_out, and_8_out, not_1_out,
       not_2_out, or_1_out, or_2_out, or_3_out, or_4_out;

  not not_1 (not_1_out, load);
  not not_2 (not_2_out, not_1_out);
  and and_1 (and_1_out, \output [0], not_1_out);
  and and_2 (and_2_out, data[0], not_2_out);
  and and_3 (and_3_out, \output [1], not_1_out);
  and and_4 (and_4_out, data[1], not_2_out);
  and and_5 (and_5_out, \output [2], not_1_out);
  and and_6 (and_6_out, data[2], not_2_out);
  and and_7 (and_7_out, \output [3], not_1_out);
  and and_8 (and_8_out, data[3], not_2_out);
  or or_1 (or_1_out, and_1_out, and_2_out);
  or or_2 (or_2_out, and_3_out, and_4_out);
  or or_3 (or_3_out, and_5_out, and_6_out);
  or or_4 (or_4_out, and_7_out, and_8_out);
  D_Flip_Flop d_ff_1 (.clk(clk), .D(or_1_out), .Q(\output [0]), .reset(clr));  // open: Qn, preset, en
  D_Flip_Flop d_ff_2 (.clk(clk), .D(or_2_out), .Q(\output [1]), .reset(clr));  // open: Qn, preset, en
  D_Flip_Flop d_ff_3 (.clk(clk), .D(or_3_out), .Q(\output [2]), .reset(clr));  // open: Qn, preset, en
  D_Flip_Flop d_ff_4 (.clk(clk), .D(or_4_out), .Q(\output [3]), .reset(clr));  // open: Qn, preset, en

  // Notes on the sheet:
  //   2207053
endmodule

module _32_bit_ACC (
  input  load,
  input  [31:0] data,
  input  clk,
  input  clr,
  output [31:0] \output 
);

  _4_bit_parallel_load_register u_4_bit_parallel_load_register_1 (
    .load(load), .clr(clr), .\output (\output [3:0]), .data(data[3:0]), .clk(clk));
  _4_bit_parallel_load_register u_4_bit_parallel_load_register_2 (
    .load(load), .clr(clr), .\output (\output [7:4]), .data(data[7:4]), .clk(clk));
  _4_bit_parallel_load_register u_4_bit_parallel_load_register_3 (
    .load(load), .clr(clr), .\output (\output [11:8]), .data(data[11:8]), .clk(clk));
  _4_bit_parallel_load_register u_4_bit_parallel_load_register_4 (
    .load(load), .clr(clr), .\output (\output [15:12]), .data(data[15:12]), .clk(clk));
  _4_bit_parallel_load_register u_4_bit_parallel_load_register_5 (
    .load(load), .clr(clr), .\output (\output [19:16]), .data(data[19:16]), .clk(clk));
  _4_bit_parallel_load_register u_4_bit_parallel_load_register_6 (
    .load(load), .clr(clr), .\output (\output [23:20]), .data(data[23:20]), .clk(clk));
  _4_bit_parallel_load_register u_4_bit_parallel_load_register_7 (
    .load(load), .clr(clr), .\output (\output [27:24]), .data(data[27:24]), .clk(clk));
  _4_bit_parallel_load_register u_4_bit_parallel_load_register_8 (
    .load(load), .clr(clr), .\output (\output [31:28]), .data(data[31:28]), .clk(clk));

  // Notes on the sheet:
  //   2207053
endmodule

module _4_bit_IR (
  input  [3:0] data,
  input  load,
  input  clk,
  input  clr,
  output [3:0] \output 
);

  _4_bit_parallel_load_register u_4_bit_parallel_load_register_1 (
    .load(load), .clr(clr), .\output (\output ), .data(data), .clk(clk));

  // Notes on the sheet:
  //   2207053
endmodule

module _5_bit_PC (
  input  cnt,
  input  [4:0] data,
  input  load,
  input  clk,
  input  clr,
  output [4:0] \output ,
  output carry_out
);

  wire and_1_out, and_2_out, and_3_out, and_4_out, and_5_out, and_6_out, and_7_out, and_8_out, and_9_out,
       and_10_out, and_11_out, and_12_out, and_13_out, and_14_out, and_15_out, not_1_out, not_2_out,
       not_3_out, not_4_out, not_5_out, not_6_out, not_7_out, or_1_out, or_2_out, or_3_out, or_4_out,
       or_5_out, or_6_out, or_7_out, or_8_out, or_9_out, or_10_out;

  not not_1 (not_1_out, load);
  and and_1 (and_1_out, cnt, not_1_out);
  not not_2 (not_2_out, not_1_out);
  not not_3 (not_3_out, data[0]);
  not not_4 (not_4_out, data[1]);
  not not_5 (not_5_out, data[2]);
  not not_6 (not_6_out, data[3]);
  not not_7 (not_7_out, data[4]);
  and and_2 (and_2_out, not_2_out, data[0]);
  and and_3 (and_3_out, not_2_out, not_3_out);
  and and_4 (and_4_out, not_2_out, data[1]);
  and and_5 (and_5_out, not_2_out, not_4_out);
  and and_6 (and_6_out, not_2_out, data[2]);
  and and_7 (and_7_out, not_2_out, not_5_out);
  and and_8 (and_8_out, not_2_out, data[3]);
  and and_9 (and_9_out, not_2_out, not_6_out);
  and and_10 (and_10_out, not_2_out, data[4]);
  and and_11 (and_11_out, not_2_out, not_7_out);
  and and_12 (and_12_out, and_1_out, \output [0]);
  and and_13 (and_13_out, and_1_out, \output [0], \output [1]);
  and and_14 (and_14_out, and_1_out, \output [0], \output [1], \output [2]);
  and and_15 (and_15_out, \output [3], \output [2], \output [1], \output [0], and_1_out);
  or or_1 (or_1_out, and_2_out, and_1_out);
  or or_2 (or_2_out, and_3_out, and_1_out);
  or or_3 (or_3_out, and_4_out, and_12_out);
  or or_4 (or_4_out, and_5_out, and_12_out);
  or or_5 (or_5_out, and_6_out, and_13_out);
  or or_6 (or_6_out, and_7_out, and_13_out);
  or or_7 (or_7_out, and_8_out, and_14_out);
  or or_8 (or_8_out, and_9_out, and_14_out);
  or or_9 (or_9_out, and_10_out, and_15_out);
  or or_10 (or_10_out, and_15_out, and_11_out);
  J_K_Flip_Flop j_k_ff_1 (.J(or_1_out), .clk(clk), .K(or_2_out), .Q(\output [0]), .reset(clr));  // open: Qn, preset, en
  J_K_Flip_Flop j_k_ff_2 (.J(or_3_out), .clk(clk), .K(or_4_out), .Q(\output [1]), .reset(clr));  // open: Qn, preset, en
  J_K_Flip_Flop j_k_ff_3 (.J(or_5_out), .clk(clk), .K(or_6_out), .Q(\output [2]), .reset(clr));  // open: Qn, preset, en
  J_K_Flip_Flop j_k_ff_4 (.J(or_7_out), .clk(clk), .K(or_8_out), .Q(\output [3]), .reset(clr));  // open: Qn, preset, en
  J_K_Flip_Flop j_k_ff_5 (
    .J(or_9_out), .clk(clk), .K(or_10_out), .Q(\output [4]), .reset(clr));  // open: Qn, preset, en
  and and_16 (carry_out, \output [4], \output [3], \output [2], \output [1], \output [0], and_1_out);

  // Notes on the sheet:
  //   2207053
endmodule

module _5_bit_MAR (
  input  load,
  input  [4:0] data,
  input  clk,
  input  clr,
  output [4:0] \output 
);

  wire and_1_out, and_2_out, and_3_out, and_4_out, and_5_out, and_6_out, and_7_out, and_8_out, and_9_out,
       and_10_out, not_1_out, not_2_out, or_1_out, or_2_out, or_3_out, or_4_out, or_5_out;

  not not_1 (not_1_out, load);
  not not_2 (not_2_out, not_1_out);
  and and_1 (and_1_out, \output [0], not_1_out);
  and and_2 (and_2_out, data[0], not_2_out);
  and and_3 (and_3_out, \output [1], not_1_out);
  and and_4 (and_4_out, data[1], not_2_out);
  and and_5 (and_5_out, \output [2], not_1_out);
  and and_6 (and_6_out, data[2], not_2_out);
  and and_7 (and_7_out, \output [3], not_1_out);
  and and_8 (and_8_out, data[3], not_2_out);
  and and_9 (and_9_out, \output [4], not_1_out);
  and and_10 (and_10_out, data[4], not_2_out);
  or or_1 (or_1_out, and_1_out, and_2_out);
  or or_2 (or_2_out, and_3_out, and_4_out);
  or or_3 (or_3_out, and_5_out, and_6_out);
  or or_4 (or_4_out, and_7_out, and_8_out);
  or or_5 (or_5_out, and_9_out, and_10_out);
  D_Flip_Flop d_ff_1 (.clk(clk), .D(or_1_out), .Q(\output [0]), .reset(clr));  // open: Qn, preset, en
  D_Flip_Flop d_ff_2 (.clk(clk), .D(or_2_out), .Q(\output [1]), .reset(clr));  // open: Qn, preset, en
  D_Flip_Flop d_ff_3 (.clk(clk), .D(or_3_out), .Q(\output [2]), .reset(clr));  // open: Qn, preset, en
  D_Flip_Flop d_ff_4 (.clk(clk), .D(or_4_out), .Q(\output [3]), .reset(clr));  // open: Qn, preset, en
  D_Flip_Flop d_ff_5 (.D(or_5_out), .Q(\output [4]));  // open: clk, Qn, preset, en, reset

  // Notes on the sheet:
  //   2207053
endmodule

module _1_bit_parallel_load_register (
  input  load,
  input  i_p,
  input  clk,
  input  clr,
  output o_p
);

  wire and_1_out, and_2_out, not_1_out, not_2_out, or_1_out;

  not not_1 (not_1_out, load);
  not not_2 (not_2_out, not_1_out);
  and and_1 (and_1_out, o_p, not_1_out);
  and and_2 (and_2_out, i_p, not_2_out);
  or or_1 (or_1_out, and_1_out, and_2_out);
  D_Flip_Flop d_ff_1 (.clk(clk), .D(or_1_out), .Q(o_p), .reset(clr));  // open: Qn, preset, en

  // Notes on the sheet:
  //   2207053
endmodule

module _32_bit_MBR (
  input  count,
  input  load,
  input  clk,
  input  clear,
  input  [31:0] data,
  output [31:0] \output 
);

  wire n4_bit_counter_with_parallel_load_1_carry_out, n4_bit_counter_with_parallel_load_2_carry_out,
       n4_bit_counter_with_parallel_load_3_carry_out, n4_bit_counter_with_parallel_load_4_carry_out,
       n4_bit_counter_with_parallel_load_5_carry_out, n4_bit_counter_with_parallel_load_6_carry_out,
       n4_bit_counter_with_parallel_load_7_carry_out;

  _4_bit_counter_with_parallel_load u_4_bit_counter_with_parallel_load_1 (
    .cin(count), .cnt(count), .load(load), .clk(clk), .clr(clear), .data(data[3:0]),
    .\output (\output [3:0]), .carry_out(n4_bit_counter_with_parallel_load_1_carry_out));
  _4_bit_counter_with_parallel_load u_4_bit_counter_with_parallel_load_2 (
    .cin(n4_bit_counter_with_parallel_load_1_carry_out), .cnt(count), .load(load), .clk(clk), .clr(clear),
    .data(data[7:4]), .\output (\output [7:4]), .carry_out(n4_bit_counter_with_parallel_load_2_carry_out));
  _4_bit_counter_with_parallel_load u_4_bit_counter_with_parallel_load_3 (
    .cin(n4_bit_counter_with_parallel_load_2_carry_out), .cnt(count), .load(load), .clk(clk), .clr(clear),
    .data(data[11:8]), .\output (\output [11:8]), .carry_out(n4_bit_counter_with_parallel_load_3_carry_out));
  _4_bit_counter_with_parallel_load u_4_bit_counter_with_parallel_load_4 (
    .cin(n4_bit_counter_with_parallel_load_3_carry_out), .cnt(count), .load(load), .clk(clk), .clr(clear),
    .data(data[15:12]), .\output (\output [15:12]), .carry_out(n4_bit_counter_with_parallel_load_4_carry_out));
  _4_bit_counter_with_parallel_load u_4_bit_counter_with_parallel_load_5 (
    .cin(n4_bit_counter_with_parallel_load_4_carry_out), .cnt(count), .load(load), .clk(clk), .clr(clear),
    .data(data[19:16]), .\output (\output [19:16]), .carry_out(n4_bit_counter_with_parallel_load_5_carry_out));
  _4_bit_counter_with_parallel_load u_4_bit_counter_with_parallel_load_6 (
    .cin(n4_bit_counter_with_parallel_load_5_carry_out), .cnt(count), .load(load), .clk(clk), .clr(clear),
    .data(data[23:20]), .\output (\output [23:20]), .carry_out(n4_bit_counter_with_parallel_load_6_carry_out));
  _4_bit_counter_with_parallel_load u_4_bit_counter_with_parallel_load_7 (
    .cin(n4_bit_counter_with_parallel_load_6_carry_out), .cnt(count), .load(load), .clk(clk), .clr(clear),
    .data(data[27:24]), .\output (\output [27:24]), .carry_out(n4_bit_counter_with_parallel_load_7_carry_out));
  _4_bit_counter_with_parallel_load u_4_bit_counter_with_parallel_load_8 (
    .cin(n4_bit_counter_with_parallel_load_7_carry_out), .cnt(count), .load(load), .clk(clk), .clr(clear),
    .data(data[31:28]), .\output (\output [31:28]));  // open: carry_out

  // Notes on the sheet:
  //   2207053
endmodule

// 4-bit cpl
module _4_bit_counter_with_parallel_load (
  input  cin,
  input  cnt,
  input  [3:0] data,
  input  load,
  input  clk,
  input  clr,
  output [3:0] \output ,
  output carry_out
);

  wire and_1_out, and_2_out, and_3_out, and_4_out, and_5_out, and_6_out, and_7_out, and_8_out, and_9_out,
       and_11_out, and_12_out, and_13_out, in, not_1_out, not_2_out, not_3_out, not_4_out, not_5_out,
       not_6_out, or_1_out, or_2_out, or_3_out, or_4_out, or_5_out, or_6_out, or_7_out, or_8_out;

  not not_1 (not_1_out, load);
  and and_1 (and_1_out, cnt, not_1_out);
  not not_2 (not_2_out, not_1_out);
  not not_3 (not_3_out, data[0]);
  not not_4 (not_4_out, data[1]);
  not not_5 (not_5_out, data[2]);
  not not_6 (not_6_out, data[3]);
  and and_2 (and_2_out, not_2_out, data[0]);
  and and_3 (and_3_out, not_2_out, not_3_out);
  and and_4 (and_4_out, not_2_out, data[1]);
  and and_5 (and_5_out, not_2_out, not_4_out);
  and and_6 (and_6_out, not_2_out, data[2]);
  and and_7 (and_7_out, not_2_out, not_5_out);
  and and_8 (and_8_out, not_2_out, data[3]);
  and and_9 (and_9_out, not_2_out, not_6_out);
  and and_10 (in, cin, and_1_out);
  and and_11 (and_11_out, in, \output [0]);
  and and_12 (and_12_out, in, \output [0], \output [1]);
  and and_13 (and_13_out, in, \output [0], \output [1], \output [2]);
  or or_1 (or_1_out, and_2_out, in);
  or or_2 (or_2_out, and_3_out, in);
  or or_3 (or_3_out, and_4_out, and_11_out);
  or or_4 (or_4_out, and_5_out, and_11_out);
  or or_5 (or_5_out, and_6_out, and_12_out);
  or or_6 (or_6_out, and_7_out, and_12_out);
  or or_7 (or_7_out, and_8_out, and_13_out);
  or or_8 (or_8_out, and_9_out, and_13_out);
  J_K_Flip_Flop j_k_ff_1 (.J(or_1_out), .clk(clk), .K(or_2_out), .Q(\output [0]), .reset(clr));  // open: Qn, preset, en
  J_K_Flip_Flop j_k_ff_2 (.J(or_3_out), .clk(clk), .K(or_4_out), .Q(\output [1]), .reset(clr));  // open: Qn, preset, en
  J_K_Flip_Flop j_k_ff_3 (.J(or_5_out), .clk(clk), .K(or_6_out), .Q(\output [2]), .reset(clr));  // open: Qn, preset, en
  J_K_Flip_Flop j_k_ff_4 (.J(or_7_out), .clk(clk), .K(or_8_out), .Q(\output [3]), .reset(clr));  // open: Qn, preset, en
  and and_14 (carry_out, \output [3], \output [2], \output [1], \output [0], and_1_out, in);

  // Notes on the sheet:
  //   2207053
endmodule

module ROL (
  input  [31:0] IN,
  output [31:0] OUT
);


  assign OUT = {IN[30:0], IN[31]};

  // Notes on the sheet:
  //   2207053
endmodule
